// Digital circuit alu.dig as structural Verilog
module alu (
  input  [15:0] data_right,
  input  [15:0] data_left,
  input  [3:0] op,
  input  clk,
  output [3:0] flags,
  output [15:0] res
);

  wire and_2_out, and_3_out, C, V, Z, zero_eq;
  wire [15:0] add_1_s, and_1_out, barrel_shifter_1_out, not_1_out, or_1_out, xor_1_out;

  Add #(.Bits(16)) add_1 (.a(data_left), .b(data_right), .c_i(1'b0), .s(add_1_s), .c_o(C));
  assign and_1_out = data_left & data_right;  // And and_1, 16 bits wide
  assign or_1_out = data_left | data_right;  // Or or_1, 16 bits wide
  assign xor_1_out = data_left ^ data_right;  // XOr xor_1, 16 bits wide
  barrel_shifter barrel_shifter_1 (
    .n(data_left[3:0]), .asr(1'b0), .shl(1'b0), .in(data_right), .out(barrel_shifter_1_out));
  assign not_1_out = ~data_right;  // Not not_1, 16 bits wide
  Register #(.Bits(4)) u_flags (.D({res[15], V, Z, C}), .C(clk), .en(1'b1), .Q(flags));
  Multiplexer #(.Bits(16), .Selector_Bits(4)) multiplexer_1 (
    .sel(op), .in_0(add_1_s), .in_1(add_1_s), .in_2(add_1_s), .in_3(add_1_s), .in_4(and_1_out),
    .in_5(or_1_out), .in_6(xor_1_out), .in_7(barrel_shifter_1_out), .in_8(barrel_shifter_1_out),
    .in_9(barrel_shifter_1_out), .in_10(data_left), .in_11(data_right), .in_12(not_1_out), .in_13(add_1_s),
    .in_14(add_1_s), .in_15(add_1_s), .out(res));
  Comparator #(.Bits(16)) zero (.a(res), .b({16{1'b0}}), .eq(zero_eq));  // open: gt, lt
  not not_2 (Z, zero_eq);
  and and_2 (and_2_out, data_left[15], data_right[15], ~res[15]);  // And
  and and_3 (and_3_out, ~data_left[15], ~data_right[15], res[15]);  // And
  or or_2 (V, and_2_out, and_3_out);

  // Other names for the same wires on the sheet: L[15:0] = data_left; LS = data_left[15]; R[15:0] = data_right;
  //   RS = data_right[15]; S = res[15]
endmodule
