// Digital circuit barrel_shifter.dig as structural Verilog
module barrel_shifter (
  input  [3:0] n,
  input  asr,
  input  shl,
  input  [15:0] in,
  output [15:0] out
);

  wire multiplexer_1_out, multiplexer_2_out, multiplexer_3_out, multiplexer_4_out, multiplexer_5_out,
       multiplexer_6_out, multiplexer_7_out, multiplexer_8_out, multiplexer_9_out, multiplexer_10_out,
       multiplexer_11_out, multiplexer_13_out, multiplexer_14_out, multiplexer_15_out, multiplexer_16_out,
       multiplexer_17_out, multiplexer_18_out, multiplexer_19_out, multiplexer_21_out, multiplexer_22_out,
       multiplexer_23_out, multiplexer_24_out, multiplexer_25_out, multiplexer_26_out, multiplexer_29_out,
       multiplexer_30_out, multiplexer_31_out, multiplexer_32_out, multiplexer_33_out, multiplexer_34_out,
       multiplexer_35_out, multiplexer_37_out, multiplexer_38_out, multiplexer_39_out, multiplexer_40_out,
       multiplexer_41_out, multiplexer_42_out, multiplexer_43_out, multiplexer_45_out, multiplexer_46_out,
       multiplexer_47_out, multiplexer_48_out, multiplexer_49_out, multiplexer_50_out, multiplexer_53_out,
       multiplexer_54_out, multiplexer_55_out, multiplexer_56_out, multiplexer_57_out, multiplexer_58_out,
       multiplexer_59_out, multiplexer_61_out, multiplexer_62_out, multiplexer_63_out, multiplexer_64_out,
       multiplexer_65_out, multiplexer_66_out, multiplexer_67_out, multiplexer_69_out, multiplexer_70_out,
       multiplexer_71_out, multiplexer_72_out, multiplexer_73_out, multiplexer_74_out, multiplexer_77_out,
       multiplexer_78_out, multiplexer_79_out, multiplexer_80_out, multiplexer_81_out, multiplexer_82_out,
       multiplexer_83_out, multiplexer_85_out, multiplexer_86_out, multiplexer_87_out, multiplexer_88_out,
       multiplexer_89_out, multiplexer_90_out, multiplexer_91_out, multiplexer_93_out, multiplexer_94_out,
       multiplexer_95_out, not_1_out, not_2_out;
  wire [3:0] not_3_out;

  not not_1 (not_1_out, shl);
  not not_2 (not_2_out, asr);
  Multiplexer multiplexer_1 (.sel(not_2_out), .in_0(multiplexer_2_out), .in_1(1'b0), .out(multiplexer_1_out));
  assign not_3_out = ~n;  // Not not_3, 4 bits wide
  Multiplexer multiplexer_2 (.sel(not_1_out), .in_0(in[0]), .in_1(in[15]), .out(multiplexer_2_out));
  Multiplexer multiplexer_3 (
    .sel(not_3_out[3]), .in_0(multiplexer_1_out), .in_1(multiplexer_2_out), .out(multiplexer_3_out));
  Multiplexer multiplexer_4 (
    .sel(not_3_out[2]), .in_0(multiplexer_1_out), .in_1(multiplexer_3_out), .out(multiplexer_4_out));
  Multiplexer multiplexer_5 (.sel(not_1_out), .in_0(in[2]), .in_1(in[13]), .out(multiplexer_5_out));
  Multiplexer multiplexer_6 (.sel(not_1_out), .in_0(in[1]), .in_1(in[14]), .out(multiplexer_6_out));
  Multiplexer multiplexer_7 (
    .sel(not_3_out[3]), .in_0(multiplexer_1_out), .in_1(multiplexer_6_out), .out(multiplexer_7_out));
  Multiplexer multiplexer_8 (
    .sel(not_3_out[2]), .in_0(multiplexer_1_out), .in_1(multiplexer_7_out), .out(multiplexer_8_out));
  Multiplexer multiplexer_9 (
    .sel(not_3_out[1]), .in_0(multiplexer_1_out), .in_1(multiplexer_4_out), .out(multiplexer_9_out));
  Multiplexer multiplexer_10 (
    .sel(not_3_out[1]), .in_0(multiplexer_1_out), .in_1(multiplexer_8_out), .out(multiplexer_10_out));
  Multiplexer multiplexer_11 (
    .sel(not_3_out[0]), .in_0(multiplexer_1_out), .in_1(multiplexer_9_out), .out(multiplexer_11_out));
  Multiplexer multiplexer_12 (.sel(not_1_out), .in_0(multiplexer_95_out), .in_1(multiplexer_11_out), .out(out[15]));
  Multiplexer multiplexer_13 (.sel(not_1_out), .in_0(in[3]), .in_1(in[12]), .out(multiplexer_13_out));
  Multiplexer multiplexer_14 (
    .sel(not_3_out[3]), .in_0(multiplexer_1_out), .in_1(multiplexer_5_out), .out(multiplexer_14_out));
  Multiplexer multiplexer_15 (
    .sel(not_3_out[3]), .in_0(multiplexer_1_out), .in_1(multiplexer_13_out), .out(multiplexer_15_out));
  Multiplexer multiplexer_16 (
    .sel(not_3_out[2]), .in_0(multiplexer_1_out), .in_1(multiplexer_14_out), .out(multiplexer_16_out));
  Multiplexer multiplexer_17 (
    .sel(not_3_out[1]), .in_0(multiplexer_4_out), .in_1(multiplexer_16_out), .out(multiplexer_17_out));
  Multiplexer multiplexer_18 (
    .sel(not_3_out[0]), .in_0(multiplexer_9_out), .in_1(multiplexer_10_out), .out(multiplexer_18_out));
  Multiplexer multiplexer_19 (
    .sel(not_3_out[0]), .in_0(multiplexer_10_out), .in_1(multiplexer_17_out), .out(multiplexer_19_out));
  Multiplexer multiplexer_20 (.sel(not_1_out), .in_0(multiplexer_91_out), .in_1(multiplexer_18_out), .out(out[14]));
  Multiplexer multiplexer_21 (.sel(not_1_out), .in_0(in[4]), .in_1(in[11]), .out(multiplexer_21_out));
  Multiplexer multiplexer_22 (
    .sel(not_3_out[3]), .in_0(multiplexer_1_out), .in_1(multiplexer_21_out), .out(multiplexer_22_out));
  Multiplexer multiplexer_23 (
    .sel(not_3_out[2]), .in_0(multiplexer_3_out), .in_1(multiplexer_22_out), .out(multiplexer_23_out));
  Multiplexer multiplexer_24 (
    .sel(not_3_out[2]), .in_0(multiplexer_1_out), .in_1(multiplexer_15_out), .out(multiplexer_24_out));
  Multiplexer multiplexer_25 (
    .sel(not_3_out[1]), .in_0(multiplexer_8_out), .in_1(multiplexer_24_out), .out(multiplexer_25_out));
  Multiplexer multiplexer_26 (
    .sel(not_3_out[0]), .in_0(multiplexer_17_out), .in_1(multiplexer_25_out), .out(multiplexer_26_out));
  Multiplexer multiplexer_27 (.sel(not_1_out), .in_0(multiplexer_90_out), .in_1(multiplexer_19_out), .out(out[13]));
  Multiplexer multiplexer_28 (.sel(not_1_out), .in_0(multiplexer_83_out), .in_1(multiplexer_26_out), .out(out[12]));
  Multiplexer multiplexer_29 (.sel(not_1_out), .in_0(in[6]), .in_1(in[9]), .out(multiplexer_29_out));
  Multiplexer multiplexer_30 (.sel(not_1_out), .in_0(in[5]), .in_1(in[10]), .out(multiplexer_30_out));
  Multiplexer multiplexer_31 (
    .sel(not_3_out[3]), .in_0(multiplexer_1_out), .in_1(multiplexer_30_out), .out(multiplexer_31_out));
  Multiplexer multiplexer_32 (
    .sel(not_3_out[2]), .in_0(multiplexer_7_out), .in_1(multiplexer_31_out), .out(multiplexer_32_out));
  Multiplexer multiplexer_33 (
    .sel(not_3_out[1]), .in_0(multiplexer_24_out), .in_1(multiplexer_32_out), .out(multiplexer_33_out));
  Multiplexer multiplexer_34 (
    .sel(not_3_out[1]), .in_0(multiplexer_16_out), .in_1(multiplexer_23_out), .out(multiplexer_34_out));
  Multiplexer multiplexer_35 (
    .sel(not_3_out[0]), .in_0(multiplexer_25_out), .in_1(multiplexer_34_out), .out(multiplexer_35_out));
  Multiplexer multiplexer_36 (.sel(not_1_out), .in_0(multiplexer_74_out), .in_1(multiplexer_35_out), .out(out[11]));
  Multiplexer multiplexer_37 (.sel(not_1_out), .in_0(in[7]), .in_1(in[8]), .out(multiplexer_37_out));
  Multiplexer multiplexer_38 (
    .sel(not_3_out[3]), .in_0(multiplexer_1_out), .in_1(multiplexer_29_out), .out(multiplexer_38_out));
  Multiplexer multiplexer_39 (
    .sel(not_3_out[3]), .in_0(multiplexer_1_out), .in_1(multiplexer_37_out), .out(multiplexer_39_out));
  Multiplexer multiplexer_40 (
    .sel(not_3_out[2]), .in_0(multiplexer_14_out), .in_1(multiplexer_38_out), .out(multiplexer_40_out));
  Multiplexer multiplexer_41 (
    .sel(not_3_out[1]), .in_0(multiplexer_23_out), .in_1(multiplexer_40_out), .out(multiplexer_41_out));
  Multiplexer multiplexer_42 (
    .sel(not_3_out[0]), .in_0(multiplexer_34_out), .in_1(multiplexer_33_out), .out(multiplexer_42_out));
  Multiplexer multiplexer_43 (
    .sel(not_3_out[0]), .in_0(multiplexer_33_out), .in_1(multiplexer_41_out), .out(multiplexer_43_out));
  Multiplexer multiplexer_44 (.sel(not_1_out), .in_0(multiplexer_67_out), .in_1(multiplexer_42_out), .out(out[10]));
  Multiplexer multiplexer_45 (.sel(not_1_out), .in_0(in[8]), .in_1(in[7]), .out(multiplexer_45_out));
  Multiplexer multiplexer_46 (
    .sel(not_3_out[3]), .in_0(multiplexer_2_out), .in_1(multiplexer_45_out), .out(multiplexer_46_out));
  Multiplexer multiplexer_47 (
    .sel(not_3_out[2]), .in_0(multiplexer_22_out), .in_1(multiplexer_46_out), .out(multiplexer_47_out));
  Multiplexer multiplexer_48 (
    .sel(not_3_out[2]), .in_0(multiplexer_15_out), .in_1(multiplexer_39_out), .out(multiplexer_48_out));
  Multiplexer multiplexer_49 (
    .sel(not_3_out[1]), .in_0(multiplexer_32_out), .in_1(multiplexer_48_out), .out(multiplexer_49_out));
  Multiplexer multiplexer_50 (
    .sel(not_3_out[0]), .in_0(multiplexer_41_out), .in_1(multiplexer_49_out), .out(multiplexer_50_out));
  Multiplexer multiplexer_51 (.sel(not_1_out), .in_0(multiplexer_66_out), .in_1(multiplexer_43_out), .out(out[9]));
  Multiplexer multiplexer_52 (.sel(not_1_out), .in_0(multiplexer_59_out), .in_1(multiplexer_50_out), .out(out[8]));
  Multiplexer multiplexer_53 (.sel(not_1_out), .in_0(in[10]), .in_1(in[5]), .out(multiplexer_53_out));
  Multiplexer multiplexer_54 (.sel(not_1_out), .in_0(in[9]), .in_1(in[6]), .out(multiplexer_54_out));
  Multiplexer multiplexer_55 (
    .sel(not_3_out[3]), .in_0(multiplexer_6_out), .in_1(multiplexer_54_out), .out(multiplexer_55_out));
  Multiplexer multiplexer_56 (
    .sel(not_3_out[2]), .in_0(multiplexer_31_out), .in_1(multiplexer_55_out), .out(multiplexer_56_out));
  Multiplexer multiplexer_57 (
    .sel(not_3_out[1]), .in_0(multiplexer_48_out), .in_1(multiplexer_56_out), .out(multiplexer_57_out));
  Multiplexer multiplexer_58 (
    .sel(not_3_out[1]), .in_0(multiplexer_40_out), .in_1(multiplexer_47_out), .out(multiplexer_58_out));
  Multiplexer multiplexer_59 (
    .sel(not_3_out[0]), .in_0(multiplexer_49_out), .in_1(multiplexer_58_out), .out(multiplexer_59_out));
  Multiplexer multiplexer_60 (.sel(not_1_out), .in_0(multiplexer_50_out), .in_1(multiplexer_59_out), .out(out[7]));
  Multiplexer multiplexer_61 (.sel(not_1_out), .in_0(in[11]), .in_1(in[4]), .out(multiplexer_61_out));
  Multiplexer multiplexer_62 (
    .sel(not_3_out[3]), .in_0(multiplexer_5_out), .in_1(multiplexer_53_out), .out(multiplexer_62_out));
  Multiplexer multiplexer_63 (
    .sel(not_3_out[3]), .in_0(multiplexer_13_out), .in_1(multiplexer_61_out), .out(multiplexer_63_out));
  Multiplexer multiplexer_64 (
    .sel(not_3_out[2]), .in_0(multiplexer_38_out), .in_1(multiplexer_62_out), .out(multiplexer_64_out));
  Multiplexer multiplexer_65 (
    .sel(not_3_out[1]), .in_0(multiplexer_47_out), .in_1(multiplexer_64_out), .out(multiplexer_65_out));
  Multiplexer multiplexer_66 (
    .sel(not_3_out[0]), .in_0(multiplexer_58_out), .in_1(multiplexer_57_out), .out(multiplexer_66_out));
  Multiplexer multiplexer_67 (
    .sel(not_3_out[0]), .in_0(multiplexer_57_out), .in_1(multiplexer_65_out), .out(multiplexer_67_out));
  Multiplexer multiplexer_68 (.sel(not_1_out), .in_0(multiplexer_43_out), .in_1(multiplexer_66_out), .out(out[6]));
  Multiplexer multiplexer_69 (.sel(not_1_out), .in_0(in[12]), .in_1(in[3]), .out(multiplexer_69_out));
  Multiplexer multiplexer_70 (
    .sel(not_3_out[3]), .in_0(multiplexer_21_out), .in_1(multiplexer_69_out), .out(multiplexer_70_out));
  Multiplexer multiplexer_71 (
    .sel(not_3_out[2]), .in_0(multiplexer_46_out), .in_1(multiplexer_70_out), .out(multiplexer_71_out));
  Multiplexer multiplexer_72 (
    .sel(not_3_out[2]), .in_0(multiplexer_39_out), .in_1(multiplexer_63_out), .out(multiplexer_72_out));
  Multiplexer multiplexer_73 (
    .sel(not_3_out[1]), .in_0(multiplexer_56_out), .in_1(multiplexer_72_out), .out(multiplexer_73_out));
  Multiplexer multiplexer_74 (
    .sel(not_3_out[0]), .in_0(multiplexer_65_out), .in_1(multiplexer_73_out), .out(multiplexer_74_out));
  Multiplexer multiplexer_75 (.sel(not_1_out), .in_0(multiplexer_42_out), .in_1(multiplexer_67_out), .out(out[5]));
  Multiplexer multiplexer_76 (.sel(not_1_out), .in_0(multiplexer_35_out), .in_1(multiplexer_74_out), .out(out[4]));
  Multiplexer multiplexer_77 (.sel(not_1_out), .in_0(in[14]), .in_1(in[1]), .out(multiplexer_77_out));
  Multiplexer multiplexer_78 (.sel(not_1_out), .in_0(in[13]), .in_1(in[2]), .out(multiplexer_78_out));
  Multiplexer multiplexer_79 (
    .sel(not_3_out[3]), .in_0(multiplexer_30_out), .in_1(multiplexer_78_out), .out(multiplexer_79_out));
  Multiplexer multiplexer_80 (
    .sel(not_3_out[2]), .in_0(multiplexer_55_out), .in_1(multiplexer_79_out), .out(multiplexer_80_out));
  Multiplexer multiplexer_81 (
    .sel(not_3_out[1]), .in_0(multiplexer_72_out), .in_1(multiplexer_80_out), .out(multiplexer_81_out));
  Multiplexer multiplexer_82 (
    .sel(not_3_out[1]), .in_0(multiplexer_64_out), .in_1(multiplexer_71_out), .out(multiplexer_82_out));
  Multiplexer multiplexer_83 (
    .sel(not_3_out[0]), .in_0(multiplexer_73_out), .in_1(multiplexer_82_out), .out(multiplexer_83_out));
  Multiplexer multiplexer_84 (.sel(not_1_out), .in_0(multiplexer_26_out), .in_1(multiplexer_83_out), .out(out[3]));
  Multiplexer multiplexer_85 (.sel(not_1_out), .in_0(in[15]), .in_1(in[0]), .out(multiplexer_85_out));
  Multiplexer multiplexer_86 (
    .sel(not_3_out[3]), .in_0(multiplexer_29_out), .in_1(multiplexer_77_out), .out(multiplexer_86_out));
  Multiplexer multiplexer_87 (
    .sel(not_3_out[3]), .in_0(multiplexer_37_out), .in_1(multiplexer_85_out), .out(multiplexer_87_out));
  Multiplexer multiplexer_88 (
    .sel(not_3_out[2]), .in_0(multiplexer_62_out), .in_1(multiplexer_86_out), .out(multiplexer_88_out));
  Multiplexer multiplexer_89 (
    .sel(not_3_out[1]), .in_0(multiplexer_71_out), .in_1(multiplexer_88_out), .out(multiplexer_89_out));
  Multiplexer multiplexer_90 (
    .sel(not_3_out[0]), .in_0(multiplexer_82_out), .in_1(multiplexer_81_out), .out(multiplexer_90_out));
  Multiplexer multiplexer_91 (
    .sel(not_3_out[0]), .in_0(multiplexer_81_out), .in_1(multiplexer_89_out), .out(multiplexer_91_out));
  Multiplexer multiplexer_92 (.sel(not_1_out), .in_0(multiplexer_19_out), .in_1(multiplexer_90_out), .out(out[2]));
  Multiplexer multiplexer_93 (
    .sel(not_3_out[2]), .in_0(multiplexer_63_out), .in_1(multiplexer_87_out), .out(multiplexer_93_out));
  Multiplexer multiplexer_94 (
    .sel(not_3_out[1]), .in_0(multiplexer_80_out), .in_1(multiplexer_93_out), .out(multiplexer_94_out));
  Multiplexer multiplexer_95 (
    .sel(not_3_out[0]), .in_0(multiplexer_89_out), .in_1(multiplexer_94_out), .out(multiplexer_95_out));
  Multiplexer multiplexer_96 (.sel(not_1_out), .in_0(multiplexer_11_out), .in_1(multiplexer_95_out), .out(out[0]));
  Multiplexer multiplexer_97 (.sel(not_1_out), .in_0(multiplexer_18_out), .in_1(multiplexer_91_out), .out(out[1]));
endmodule
