// Digital circuit byte_addressing.dig as structural Verilog
module byte_addressing (
  input  [15:0] addr,
  input  z_ns,
  input  w_nb,
  output [15:0] out_4
);

  wire [7:0] multiplexer_1_out;
  wire [15:0] bitextender_1_out, multiplexer_2_out, ramsingleportsel_1_d;

  // Probe on addr
  RAMSinglePortSel #(.AddrBits(15), .Bits(8)) ramsingleportsel_1 (
    .A(addr[14:0]), .CS(1'b1), .WE(1'b0), .OE(1'b1), .D(ramsingleportsel_1_d[7:0]));
  RAMSinglePortSel #(.AddrBits(15), .Bits(8)) ramsingleportsel_2 (
    .A(addr[14:0]), .CS(1'b1), .WE(1'b0), .OE(1'b1), .D(ramsingleportsel_1_d[15:8]));
  Multiplexer #(.Bits(8)) multiplexer_1 (
    .sel(addr[15]), .in_0(ramsingleportsel_1_d[7:0]), .in_1(ramsingleportsel_1_d[15:8]),
    .out(multiplexer_1_out));
  BitExtender bitextender_1 (.in(multiplexer_1_out), .out(bitextender_1_out));
  Multiplexer #(.Bits(16)) multiplexer_2 (
    .sel(z_ns), .in_0(bitextender_1_out), .in_1({{8{1'b0}}, multiplexer_1_out}), .out(multiplexer_2_out));
  Multiplexer #(.Bits(16)) multiplexer_3 (
    .sel(w_nb), .in_0(multiplexer_2_out), .in_1(ramsingleportsel_1_d), .out(out_4));
endmodule
