// Digital circuit cpu.dig as structural Verilog
module cpu (
  input  clk
);

  wire alu, decode_1_p3, decode_1_p4, decode_1_p5, jmp_en;
  wire [1:0] w_ram, wb_sel;
  wire [2:0] cond;
  wire [3:0] alu_1_p4, decode_1_p6, decode_1_p7;
  wire [15:0] decode_1_p8, fetch_1_inst, memory_1_q, pc, regfile_1_data_left, regfile_1_data_right,
       regfile_1_data_src, res, writeback_1_data_wb;

  fetch fetch_1 (.jmp_en(jmp_en), .dst(res), .clk(clk), .pc(pc), .inst(fetch_1_inst));
  // decode decode_1: pin names not known; wires that end beside it: fetch_1_inst, cond, decode_1_p3, decode_1_p4, decode_1_p5, decode_1_p6, decode_1_p7, decode_1_p8, alu, w_ram, wb_sel
  regfile regfile_1 (
    .data_in(writeback_1_data_wb), .clk(clk), .pc(pc), .write_en(decode_1_p3), .left_sel(decode_1_p4),
    .right_sel(decode_1_p5), .reg_src(decode_1_p6), .reg_dst(decode_1_p7), .imm(decode_1_p8),
    .data_left(regfile_1_data_left), .data_right(regfile_1_data_right), .data_src(regfile_1_data_src));
  // alu alu_1: pin names not known; wires that end beside it: regfile_1_data_left, regfile_1_data_right, alu, alu_1_p4, res
  jump_unit jump_unit_1 (.flags(alu_1_p4), .cond(cond), .jmp_en(jmp_en));
  memory memory_1 (.addr(res), .data(regfile_1_data_src), .we(w_ram), .q(memory_1_q));
  writeback writeback_1 (.res_alu(res), .res_mem(memory_1_q), .pc(pc), .wb_sel(wb_sel), .data_wb(writeback_1_data_wb));

  // Notes on the sheet:
  //   update decode stage to have a "link select" signal. because
  //   of jral, we need a 4th bit to capture the "never jump" state.
  //   best way to present this to the jump unit is via a 3 bit code
  //   with Never in it, then an extra signal for whether to link.
  //   So jr, jral, jal all use Always and the last two use Link Select.
endmodule
