// Digital circuit decode.dig as structural Verilog
module decode (
  input  [15:0] instr,
  output [2:0] cond,
  output write_reg,
  output left_sel,
  output right_sel,
  output [3:0] reg_src,
  output [3:0] reg_dst,
  output [15:0] imm,
  output [1:0] write_mem,
  output [1:0] wb_sel,
  output [1:0] read_mem,
  output [3:0] alu_op
);

  wire [31:14] rom_1_d;

  ROM #(.AddrBits(16), .Bits(32)) rom_1 (
    .A(instr), .sel(1'b1),
    .D({rom_1_d[31:26], wb_sel, read_mem, write_mem, alu_op, rom_1_d[15:14], reg_dst, reg_src, right_sel, left_sel, write_reg, cond}));
  Multiplexer #(.Bits(16), .Selector_Bits(2)) multiplexer_1 (
    .sel(rom_1_d[15:14]), .in_0({{13{instr[7]}}, instr[6:4]}),
    .in_1({{11{instr[7]}}, instr[13:12], instr[6:4]}),
    .in_2({{7{instr[7]}}, instr[11], instr[4], instr[15:12], instr[6:5], 1'b0}),
    .in_3({instr[7:5], instr[3:2], instr[14:12], instr[4], instr[15], {6{1'b0}}}), .out(imm));

  // Other names for the same wires on the sheet: ten[15:6] = {instr[7:5], instr[3:2], instr[14:12], instr[4], instr[15]};
  //   four[15:0] = {{13{instr[7]}}, instr[6:4]};
  //   nine[15:1] = {{7{instr[7]}}, instr[11], instr[4], instr[15:12], instr[6:5]};
  //   six[15:0] = {{11{instr[7]}}, instr[13:12], instr[6:4]}

  // Notes on the sheet:
  //   rom_1 loads bwb16_control_rom.bin
  //   Determine where b0
  //   should come from
endmodule
