// Digital circuit fetch.dig as structural Verilog
module fetch (
  input  jmp_en,
  input  [15:0] dst,
  input  clk,
  output [15:0] pc,
  output [15:0] inst
);

  wire [15:0] add_1_s, multiplexer_1_out;

  Multiplexer #(.Bits(16)) multiplexer_1 (.sel(jmp_en), .in_0(add_1_s), .in_1(dst), .out(multiplexer_1_out));
  Register #(.Bits(16), .isProgramCounter("true")) u_pc (.D(multiplexer_1_out), .C(clk), .en(1'b1), .Q(pc));
  Add #(.Bits(16)) add_1 (.a(16'h1), .b(pc), .c_i(1'b0), .s(add_1_s));  // open: c_o
  ROM #(.AddrBits(16), .isProgramMemory("true"), .Bits(16)) rom (.A(pc), .sel(1'b1), .D(inst));

  // Notes on the sheet:
  //   contents of rom (hex, n*v repeats v):
  //   f13d,1,2,3,4
endmodule
