// Digital circuit memory.dig as structural Verilog
module memory (
  input  [15:0] addr,
  input  [1:0] we,
  input  [15:0] data,
  output [15:0] q
);

  RAMAsync #(.AddrBits(16), .Bits(8)) Data_Mem_Lo (.A(addr), .D(data[7:0]), .we(we[0]), .Q(q[7:0]));
  RAMAsync #(.AddrBits(16), .Bits(8)) Data_Mem_Hi (.A(addr), .D(data[15:8]), .we(we[1]), .Q(q[15:8]));
endmodule
