// Digital circuit regfile.dig as structural Verilog
module regfile (
  input  [15:0] data_in,
  input  clk,
  input  [15:0] pc,
  input  write_en,
  input  left_sel,
  input  right_sel,
  input  [3:0] reg_src,
  input  [3:0] reg_dst,
  input  [15:0] imm,
  output [15:0] data_left,
  output [15:0] data_right,
  output [15:0] data_src
);

  wire [15:0] registerfile_1_db;

  RegisterFile #(.AddrBits(4), .Bits(16)) registerfile_1 (
    .Din(data_in), .we(write_en), .Rw(reg_dst), .C(clk), .Ra(reg_src), .Rb(reg_dst), .Da(data_src),
    .Db(registerfile_1_db));
  Multiplexer #(.Bits(16)) multiplexer_1 (.sel(left_sel), .in_0(data_src), .in_1(pc), .out(data_left));
  Multiplexer #(.Bits(16)) multiplexer_2 (.sel(right_sel), .in_0(registerfile_1_db), .in_1(imm), .out(data_right));
endmodule
