// Digital circuit writeback.dig as structural Verilog
module writeback (
  input  [15:0] alu,
  input  [15:0] mem,
  input  [15:0] pc,
  input  [1:0] wb_sel,
  output [15:0] data_wb
);

  Multiplexer #(.Selector_Bits(2), .Bits(16)) multiplexer_1 (
    .sel(wb_sel), .in_0(mem), .in_1(alu), .in_2(pc), .in_3(pc), .out(data_wb));
endmodule
